// Logisim project control.circ as structural Verilog: 1 circuit, main circuit main
module main (
  input  j,
  input  i,
  input  enb,
  input  clk,
  input  reset,
  output s1,
  output s2,
  output enb1,
  output enb0
);

  wire and_1_out, and_2_out, and_3_out, and_4_out, and_5_out, and_6_out, and_7_out, n0_q, n0_qn, n1_q, n1_qn,
       n2_q, n2_qn, or_1_out, or_2_out;

  D_Flip_Flop n2 (.clk(clk), .D(or_1_out), .Q(n2_q), .Qn(n2_qn), .en(enb), .reset(reset));  // open: preset
  D_Flip_Flop n1 (.clk(clk), .D(and_6_out), .Q(n1_q), .Qn(n1_qn), .en(enb), .reset(reset));  // open: preset
  D_Flip_Flop n0 (.clk(clk), .D(or_2_out), .Q(n0_q), .Qn(n0_qn), .en(enb), .reset(reset));  // open: preset
  and and_1 (and_1_out, j, n2_q, n1_qn, n0_qn);
  and and_2 (and_2_out, n2_qn, n1_q, n0_qn);
  and and_3 (and_3_out, n2_q, n1_qn, n0_qn);
  and and_4 (and_4_out, n2_qn, n1_qn, n0_qn);
  and and_5 (and_5_out, n2_qn, n1_qn, n0_q, i);
  or or_1 (or_1_out, and_1_out, and_7_out, and_2_out);
  and and_6 (and_6_out, n2_qn, n0_q);
  or or_2 (or_2_out, and_3_out, and_4_out, and_5_out, and_7_out);
  and and_7 (and_7_out, n2_q, n1_qn, n0_q);
  and and_8 (s1, n2_qn, n1_qn, n0_qn);
  and and_9 (s2, n2_q, n1_qn, n0_qn);
  and and_10 (enb1, n0_q, n1_qn, n2_qn);
  or or_3 (enb0, enb1, s1);
endmodule
