// Logisim project datapath.circ as structural Verilog
module adder (
  input  c,
  input  a,
  input  b,
  output s,
  output ci_1
);

  wire and_1_out, and_2_out, and_3_out, not_1_out, not_2_out, or_1_out, or_3_out;

  or or_1 (or_1_out, a, b);
  and and_1 (and_1_out, b, a);
  not not_1 (not_1_out, and_1_out);
  and and_2 (and_2_out, or_1_out, not_1_out);
  or or_2 (ci_1, and_1_out, and_3_out);
  or or_3 (or_3_out, c, and_2_out);
  and and_3 (and_3_out, c, and_2_out);
  not not_2 (not_2_out, and_3_out);
  and and_4 (s, or_3_out, not_2_out);
endmodule

module _4bit_adder (
  input  [3:0] a,
  input  c,
  input  [3:0] b,
  output [3:0] s,
  output cout
);

  wire adder_1_ci_1, adder_2_ci_1, adder_3_ci_1;

  adder adder_1 (.c(c), .a(a[0]), .b(b[0]), .s(s[0]), .ci_1(adder_1_ci_1));
  adder adder_2 (.c(adder_1_ci_1), .a(a[1]), .b(b[1]), .s(s[1]), .ci_1(adder_2_ci_1));
  adder adder_3 (.c(adder_2_ci_1), .a(a[2]), .b(b[2]), .s(s[2]), .ci_1(adder_3_ci_1));
  adder adder_4 (.c(adder_3_ci_1), .a(a[3]), .b(b[3]), .s(s[3]), .ci_1(cout));
endmodule

module _16bit_adder (
  input  [15:0] b,
  input  [15:0] a,
  input  cin,
  output [15:0] s,
  output cout
);

  wire n4bit_adder_1_cout, n4bit_adder_2_cout, n4bit_adder_3_cout;

  _4bit_adder u_4bit_adder_1 (.a(a[3:0]), .c(cin), .b(b[3:0]), .s(s[3:0]), .cout(n4bit_adder_1_cout));
  _4bit_adder u_4bit_adder_2 (.a(a[7:4]), .c(n4bit_adder_1_cout), .b(b[7:4]), .s(s[7:4]), .cout(n4bit_adder_2_cout));
  _4bit_adder u_4bit_adder_3 (.a(a[11:8]), .c(n4bit_adder_2_cout), .b(b[11:8]), .s(s[11:8]), .cout(n4bit_adder_3_cout));
  _4bit_adder u_4bit_adder_4 (.a(a[15:12]), .c(n4bit_adder_3_cout), .b(b[15:12]), .s(s[15:12]), .cout(cout));
endmodule

// adder
module _32bit_adder (
  input  in_1,
  input  [31:0] a,
  input  [31:0] b,
  output [31:0] out_4,
  output cout
);

  wire n16bit_adder_1_cout;

  _16bit_adder u_16bit_adder_1 (.b(b[15:0]), .a(a[15:0]), .cin(in_1), .s(out_4[15:0]), .cout(n16bit_adder_1_cout));
  _16bit_adder u_16bit_adder_2 (.b(b[31:16]), .a(a[31:16]), .cin(n16bit_adder_1_cout), .s(out_4[31:16]), .cout(cout));
endmodule

module shifter (
  input  [31:0] in_1,
  input  [31:0] in_2,
  output i,
  output [31:0] out_4,
  output [31:0] out_5
);

  wire [31:31] shifter_1_out;

  Shifter #(.width(32), .shift("lr")) shifter_1 (.in(in_1), .\dist (5'b00001), .out({shifter_1_out[31], out_4[30:0]}));
  Shifter #(.width(32), .shift("lr")) shifter_2 (.in(in_2), .\dist (5'b00001), .out(out_5));

  assign i = in_1[0];
  assign out_4[31] = in_2[0];
endmodule

module datap (
  input  [31:0] in_1,
  input  s1,
  input  [31:0] in_3,
  input  s2,
  input  enb0,
  input  enb1,
  input  enbc,
  input  clk,
  input  clr,
  output [31:0] out_10,
  output i,
  output [31:0] out_12,
  output j
);

  wire not_1_out, not_3_out, not_4_out, not_5_out;
  wire [5:0] counter_1_q;
  wire [31:0] multiplexer_1_out, multiplexer_2_out, n32bit_adder_1_out_4, shifter_1_out_4, shifter_1_out_5;

  Multiplexer #(.width(32), .enable("false")) multiplexer_1 (
    .in0(shifter_1_out_4), .in1(in_1), .out(multiplexer_1_out), .sel(s1));
  Register #(.width(32)) register_1 (.D(multiplexer_1_out), .en(enb0), .Q(out_10), .clk(clk), .clr(clr));
  Register #(.width(32)) register_2 (.D(shifter_1_out_5), .en(enb1), .Q(out_12), .clk(clk), .clr(clr));
  Counter #(.width(6), .max('h20)) counter_1 (
    .count(enbc), .Q(counter_1_q), .clk(clk), .clr(clr));  // open: load, D, carry
  Multiplexer #(.width(32), .enable("false")) multiplexer_2 (
    .in0(out_12), .in1(n32bit_adder_1_out_4), .out(multiplexer_2_out), .sel(i));
  _32bit_adder u_32bit_adder_1 (.in_1(1'b0), .a(out_12), .b(in_3), .out_4(n32bit_adder_1_out_4));  // open: cout
  not not_1 (not_1_out, counter_1_q[0]);
  not not_2 (not_1_out, counter_1_q[1]);
  not not_3 (not_3_out, counter_1_q[2]);
  not not_4 (not_4_out, counter_1_q[3]);
  shifter shifter_1 (.in_1(out_10), .in_2(multiplexer_2_out), .i(i), .out_4(shifter_1_out_4), .out_5(shifter_1_out_5));
  and and_1 (j, not_1_out, not_1_out, not_3_out, not_5_out, counter_1_q[5]);
  not not_5 (not_5_out, counter_1_q[4]);
endmodule
