// Logisim project mult32.circ as structural Verilog: 1 circuit, main circuit main
module main (
  input  [31:0] a,
  input  [31:0] b,
  input  clear,
  output [31:0] product_lsb32,
  output [31:0] product_msb32
);

  wire clk_out, datap_1_i, datap_1_j, main_1_enb0, main_1_enb1, main_1_s1, main_1_s2;

  Clock clk (.out(clk_out));
  datap datap_1 (
    .in_1(a), .in_3(b), .enb0(main_1_enb0), .enb1(main_1_enb1), .enbc(main_1_enb1), .clk(clk_out),
    .clr(clear), .s1(main_1_s1), .s2(main_1_s2), .out_10(product_lsb32), .i(datap_1_i),
    .out_12(product_msb32), .j(datap_1_j));
  control_main main_1 (
    .j(datap_1_j), .i(datap_1_i), .enb(1'b1), .clk(clk_out), .reset(clear), .s1(main_1_s1), .s2(main_1_s2),
    .enb1(main_1_enb1), .enb0(main_1_enb0));
endmodule
